// Logisim project CPU Design.circ as structural Verilog: 3 circuits, main circuit main
module main (
);

  wire clock_1_out, EN, INC_DR, INC_PC, LD_AC, LD_AR, LD_DR, LD_IR, LD_PC, READ, T2, WRITE;
  wire [2:0] ALU_select, BUS_select;
  wire [7:0] AR_input, AR_q, bit_extender_1_out, bit_extender_2_out, IR_4_11, PC_q;
  wire [15:0] AC_q, alu_1_output, bit_extender_3_out, bit_extender_4_out, DR, IR, multiplexer_2_out,
       ram_1_data, TR_q;

  Clock clock_1 (.out(clock_1_out));
  Bit_Extender #(.in_width(16), .out_width(8)) bit_extender_1 (.in(multiplexer_2_out), .out(bit_extender_1_out));
  CU cu_1 (
    .IR(IR), .DR(DR), .CLK(clock_1_out), .ALU_select(ALU_select), .IR_4_11(IR_4_11), .LD_PC(LD_PC),
    .INC_PC(INC_PC), .EN(EN), .BUS_select(BUS_select), .READ(READ), .WRITE(WRITE), .LD_DR(LD_DR),
    .LD_IR(LD_IR), .INC_DR(INC_DR), .LD_AC(LD_AC), .T2(T2), .LD_AR(LD_AR));
  Multiplexer #(.width(8), .enable("false")) multiplexer_1 (
    .in0(bit_extender_1_out), .in1(IR_4_11), .out(AR_input), .sel(T2));
  ALU alu_1 (.DR(DR), .AC(AC_q), .C2C1C0(ALU_select), .Output(alu_1_output));
  Bit_Extender #(.in_width(16), .out_width(8)) bit_extender_2 (.in(multiplexer_2_out), .out(bit_extender_2_out));
  RAM #(.dataWidth(16), .bus("separate")) ram_1 (
    .addr(AR_q), .din(multiplexer_2_out), .data(ram_1_data), .str(WRITE), .clk(clock_1_out), .ld(READ));  // open: sel, clr
  Counter AR (.load(LD_AR), .D(AR_input), .count(1'b0), .Q(AR_q), .clk(clock_1_out), .clr(1'b0));  // open: carry
  Counter PC (
    .load(LD_PC), .D(bit_extender_2_out), .count(INC_PC), .Q(PC_q), .clk(clock_1_out), .clr(1'b0));  // open: carry
  Counter #(.width(16), .max('hffff)) u_DR (
    .load(LD_DR), .D(multiplexer_2_out), .count(INC_DR), .Q(DR), .clk(clock_1_out), .clr(1'b0));  // open: carry
  Counter #(.width(16), .max('hffff)) AC (
    .load(LD_AC), .D(alu_1_output), .count(1'b0), .Q(AC_q), .clk(clock_1_out), .clr(1'b0));  // open: carry
  Register #(.width(16)) u_IR (.D(multiplexer_2_out), .en(LD_IR), .Q(IR), .clk(clock_1_out), .clr(1'b0));
  Counter #(.width(16), .max('hffff)) TR (
    .load(1'b0), .D(multiplexer_2_out), .count(1'b0), .Q(TR_q), .clk(clock_1_out), .clr(1'b0));  // open: carry
  assign bit_extender_3_out = {{8{1'b0}}, AR_q};  // Bit_Extender bit_extender_3
  assign bit_extender_4_out = {{8{1'b0}}, PC_q};  // Bit_Extender bit_extender_4
  Multiplexer #(.select(3), .width(16), .enable("false")) multiplexer_2 (
    .in1(ram_1_data), .in2(bit_extender_3_out), .in3(bit_extender_4_out), .in4(DR), .in5(AC_q), .in6(IR),
    .in7(TR_q), .out(multiplexer_2_out), .sel(BUS_select));  // open: in0
endmodule

module ALU (
  input  [15:0] DR,
  input  [15:0] AC,
  input  [2:0] C2C1C0,
  output [15:0] Output
);

  wire [15:0] adder_1_out, divider_1_out, multiplier_1_out, not_1_out, subtractor_1_out, xor_1_out;

  Divider #(.width(16)) divider_1 (.a(DR), .b(AC), .out(divider_1_out));  // open: upper, rem
  Adder #(.width(16)) adder_1 (.a(DR), .b(AC), .out(adder_1_out));  // open: cin, cout
  Subtractor #(.width(16)) subtractor_1 (.a(DR), .b(AC), .out(subtractor_1_out));  // open: bin, bout
  Multiplier #(.width(16)) multiplier_1 (.a(DR), .b(AC), .out(multiplier_1_out));  // open: cin, cout
  assign not_1_out = ~DR;  // NOT_Gate not_1, 16 bits wide
  assign xor_1_out = DR ^ AC;  // XOR_Gate xor_1, 16 bits wide
  Multiplexer #(.select(3), .width(16), .enable("false")) multiplexer_1 (
    .in1(DR), .in2(adder_1_out), .in3(subtractor_1_out), .in4(multiplier_1_out), .in5(divider_1_out),
    .in6(not_1_out), .in7(xor_1_out), .out(Output), .sel(C2C1C0));  // open: in0
endmodule

module CU (
  input  [15:0] IR,
  input  [15:0] DR,
  input  CLK,
  output [7:0] IR_4_11,
  output [2:0] ALU_select,
  output LD_PC,
  output INC_PC,
  output EN,
  output [2:0] BUS_select,
  output READ,
  output WRITE,
  output LD_DR,
  output LD_IR,
  output INC_DR,
  output LD_AC,
  output T2,
  output LD_AR
);

  wire and_1_out, and_2_out, and_3_out, and_16_out, D0, D0T3, D0T4, D1, D1T3, D1T4, D2, D2T3, D2T4, D3, D3T3,
       D4, D5, D5T3, D5T4, D5T5, D6, D6T3, D6T5, D7, D8, D9, D10, D11, D12, D13, D14, D15, d_ff_1_q,
       or_4_out, or_5_out, or_6_out, or_7_out, or_8_out, or_9_out, or_12_out, T0, T3, T4, T5, T6, T7, Z;
  wire [2:0] counter_1_q;

  Decoder #(.select(4)) decoder_1 (
    .out0(D0), .out1(D1), .out2(D2), .out3(D3), .out4(D4), .out5(D5), .out6(D6), .out7(D7), .out8(D8),
    .out9(D9), .out10(D10), .out11(D11), .out12(D12), .out13(D13), .out14(D14), .out15(D15), .sel(IR[15:12]),
    .en(1'b1));
  or or_1 (EN, WRITE, READ);
  or or_2 (READ, D6T3, D2T3, D1T3, D0T3, D5T3, LD_IR);
  or or_3 (WRITE, D3T3, D6T5);
  or or_4 (or_4_out, D1, D2, D0);
  or or_5 (or_5_out, D3, D4);
  or or_6 (or_6_out, D6, D5);
  and and_1 (and_1_out, or_4_out, T4);
  and and_2 (and_2_out, or_5_out, T3);
  and and_3 (and_3_out, or_6_out, T5);
  Counter #(.width(3), .max('h7)) counter_1 (
    .load(1'b0), .count(1'b1), .Q(counter_1_q), .clk(CLK), .clr(d_ff_1_q));  // open: D, carry
  or or_7 (or_7_out, and_1_out, and_2_out, and_3_out);
  or or_8 (or_8_out, D3T3, D5T4);
  D_Flip_Flop d_ff_1 (.clk(CLK), .D(or_7_out), .Q(d_ff_1_q));  // open: Qn, preset, en, reset
  Priority_Encoder priority_encoder_1 (
    .in0(1'b0), .in1(READ), .in2(LD_PC), .in3(T0), .in4(D6T5), .in5(or_8_out), .in6(T2), .in7(1'b0),
    .out(BUS_select), .en_in(1'b1));  // open: gs, en_out
  Decoder #(.select(3)) decoder_2 (
    .out0(T0), .out1(LD_IR), .out2(T2), .out3(T3), .out4(T4), .out5(T5), .out6(T6), .out7(T7),
    .sel(counter_1_q), .en(1'b1));
  and and_4 (D0T3, D0, T3);
  and and_5 (D0T4, D0, T4);
  and and_6 (D2T3, D2, T3);
  and and_7 (D2T4, D2, T4);
  or or_9 (or_9_out, D2T4, D5T4);
  or or_10 (LD_DR, D2T3, D1T3, D6T3, D0T3, D5T3, D5T4);
  Priority_Encoder priority_encoder_2 (
    .in0(1'b0), .in1(or_9_out), .in2(D1T4), .in3(1'b0), .in4(1'b0), .in5(D5T5), .in6(1'b0), .in7(D0T4),
    .out(ALU_select));  // open: en_in
  and and_8 (D1T3, D1, T3);
  and and_9 (D1T4, D1, T4);
  or or_11 (LD_AR, T0, T2);
  and and_10 (D6T3, D6, T3);
  and and_11 (INC_DR, D6, T4);
  and and_12 (D6T5, D6, T5);
  or or_12 (or_12_out, DR[0], DR[1], DR[2], DR[3], DR[4], DR[5], DR[6], DR[7], DR[8], DR[9], DR[10], DR[11], DR[12], DR[13], DR[14], DR[15]);
  or or_13 (LD_AC, D2T4, D1T4, D0T4, D5T5, D5T4);
  and and_13 (D5T3, D5, T3);
  and and_14 (D5T4, D5, T4);
  and and_15 (D5T5, D5, T5);
  and and_16 (and_16_out, D6T5, Z);
  not not_1 (Z, or_12_out);
  or or_14 (INC_PC, LD_IR, and_16_out);
  and and_17 (D3T3, D3, T3);
  and and_18 (LD_PC, D4, T3);

  assign IR_4_11 = IR[11:4];

  // Other names for the same wires on the sheet: D4T3 = LD_PC; D6T4 = INC_DR; T1 = LD_IR

  // Notes on the sheet:
  //   IR
  //   MEMORY
  //   LD IR
  //   SC
  //   BUS
  //   DR
  //   ALU
  //   AR
  //   AC
  //   PC
endmodule
